# Fritzing sketch Printer (saved by Fritzing 0.9.1b)
breadboards: 1

parts:
  temp_HotEnd = female pin header, 2 pins [form="♀ (female)"]
  R1 = Resistor [tolerance=±5% resistance=4.7k package=THT]
  C1 = Electrolytic Capacitor [capacitance=10µF package="100 mil [THT, electrolytic]"]
  R2 = Resistor [tolerance=±5% resistance=4.7k package=THT]
  C2 = Electrolytic Capacitor [capacitance=10µF package="100 mil [THT, electrolytic]"]
  temp_HeatBed = female pin header, 2 pins [form="♀ (female)"]
  Endstop_X = female pin header, 2 pins [form="♀ (female)"]
  Endstop_Y = female pin header, 2 pins [form="♀ (female)"]
  Endstop_Z1 = female pin header, 2 pins [form="♀ (female)"]
  Endstop_Z2 = female pin header, 2 pins [form="♀ (female)"]
  Fan1 = Screw terminal - 2 pins [package=THT]
  Fan2 = Screw terminal - 2 pins [package=THT]
  Heatbed = Screw terminal - 2 pins [package=THT]
  Q1 = NPN-Transistor [package="TO92 [THT]"]
  Q2 = NPN-Transistor [package="TO92 [THT]"]
  R3 = Resistor [tolerance=±5% resistance=1k package=THT]
  R4 = Resistor [tolerance=±5% resistance=1k package=THT]
  Q3 = NPN-Transistor [package="TO92 [THT]"]
  Q4 = NPN-Transistor [package="TO92 [THT]"]
  R5 = Resistor [tolerance=±5% resistance=1k package=THT]
  R6 = Resistor [tolerance=±5% resistance=1k package=THT]
  Hotend = Screw terminal - 2 pins [package=THT]
  Q5 = NPN-Transistor [package="TO92 [THT]"]
  R7 = Resistor [tolerance=±5% resistance=1k package=THT]
  R8 = Resistor [tolerance=±5% resistance=1k package=THT]
  Q6 = NPN-Transistor [package="TO92 [THT]"]
  R9 = Resistor [tolerance=±5% resistance=860 package=THT]
  LED1 = LED - 5mm [color="Red (633nm)" package="5 mm [THT]"]
  R10 = Resistor [tolerance=±5% resistance=860 package=THT]
  LED2 = LED - 5mm [color="Red (633nm)" package="5 mm [THT]"]
  ATX = screw terminal, 4 pins
  Q7 = NPN-Transistor [package="TO92 [THT]"]
  Q8 = PNP-Transistor [package="TO92 [THT]"]
  Q9 = NPN-Transistor [package="TO92 [THT]"]
  Q10 = PNP-Transistor [package="TO92 [THT]"]
  D20 = Rectifier Diode [part_number=1N4148 package="300 mil [THT]"]
  D21 = Rectifier Diode [part_number=1N4148 package="300 mil [THT]"]
  D22 = Rectifier Diode [part_number=1N4148 package="300 mil [THT]"]
  D23 = Rectifier Diode [part_number=1N4148 package="300 mil [THT]"]
  R11 = Resistor [tolerance=±5% resistance=1k package=THT]
  R12 = Resistor [tolerance=±5% resistance=1k package=THT]
  R13 = Resistor [tolerance=±5% resistance=1k package=THT]
  R14 = Resistor [tolerance=±5% resistance=1k package=THT]
  R15 = Resistor [tolerance=±5% resistance=40 package=THT]
  D24 = Zener Diode [part_number=1N4732A breakdown_voltage=7.5 package="300 mil [THT]"]
  R16 = Resistor [tolerance=±5% resistance=40 package=THT]
  D25 = Zener Diode [part_number=1N4732A breakdown_voltage=7.5 package="300 mil [THT]"]
  R17 = Resistor [tolerance=±5% resistance=40 package=THT]
  D26 = Zener Diode [part_number=1N4732A breakdown_voltage=7.5 package="300 mil [THT]"]
  R18 = Resistor [tolerance=±5% resistance=40 package=THT]
  D27 = Zener Diode [part_number=1N4732A breakdown_voltage=7.5 package="300 mil [THT]"]
  Coil1_M1 = Screw terminal - 2 pins [package=THT]
  R19 = Resistor [tolerance=±5% resistance=1k package=THT]
  R20 = Resistor [tolerance=±5% resistance=1k package=THT]
  R21 = Resistor [tolerance=±5% resistance=1k package=THT]
  R22 = Resistor [tolerance=±5% resistance=1k package=THT]
  Q11 = NPN-Transistor [package="TO92 [THT]"]
  Q12 = NPN-Transistor [package="TO92 [THT]"]
  Q13 = PNP-Transistor [package="TO92 [THT]"]
  Q14 = PNP-Transistor [package="TO92 [THT]"]
  D28 = Rectifier Diode [part_number=1N4148 package="300 mil [THT]"]
  D29 = Rectifier Diode [part_number=1N4148 package="300 mil [THT]"]
  D30 = Rectifier Diode [part_number=1N4148 package="300 mil [THT]"]
  D31 = Rectifier Diode [part_number=1N4148 package="300 mil [THT]"]
  Coil2_M1 = Screw terminal - 2 pins [package=THT]
  R23 = Resistor [tolerance=±5% resistance=1k package=THT]
  R24 = Resistor [tolerance=±5% resistance=1k package=THT]
  R25 = Resistor [tolerance=±5% resistance=1k package=THT]
  R26 = Resistor [tolerance=±5% resistance=1k package=THT]
  R27 = Resistor [tolerance=±5% resistance=1k package=THT]
  R28 = Resistor [tolerance=±5% resistance=1k package=THT]
  R29 = Resistor [tolerance=±5% resistance=1k package=THT]
  R30 = Resistor [tolerance=±5% resistance=1k package=THT]
  Q15 = NPN-Transistor [package="TO92 [THT]"]
  Q16 = NPN-Transistor [package="TO92 [THT]"]
  Q17 = NPN-Transistor [package="TO92 [THT]"]
  Q18 = NPN-Transistor [package="TO92 [THT]"]
  Q19 = PNP-Transistor [package="TO92 [THT]"]
  Q20 = PNP-Transistor [package="TO92 [THT]"]
  Q21 = PNP-Transistor [package="TO92 [THT]"]
  Q22 = PNP-Transistor [package="TO92 [THT]"]
  D32 = Rectifier Diode [part_number=1N4148 package="300 mil [THT]"]
  D33 = Rectifier Diode [part_number=1N4148 package="300 mil [THT]"]
  D34 = Rectifier Diode [part_number=1N4148 package="300 mil [THT]"]
  D35 = Rectifier Diode [part_number=1N4148 package="300 mil [THT]"]
  D36 = Rectifier Diode [part_number=1N4148 package="300 mil [THT]"]
  D37 = Rectifier Diode [part_number=1N4148 package="300 mil [THT]"]
  D38 = Rectifier Diode [part_number=1N4148 package="300 mil [THT]"]
  D39 = Rectifier Diode [part_number=1N4148 package="300 mil [THT]"]
  Coil1_M2 = Screw terminal - 2 pins [package=THT]
  Coil2_M2 = Screw terminal - 2 pins [package=THT]
  R31 = Resistor [tolerance=±5% resistance=1k package=THT]
  R32 = Resistor [tolerance=±5% resistance=1k package=THT]
  R33 = Resistor [tolerance=±5% resistance=1k package=THT]
  R34 = Resistor [tolerance=±5% resistance=1k package=THT]
  R35 = Resistor [tolerance=±5% resistance=1k package=THT]
  R36 = Resistor [tolerance=±5% resistance=1k package=THT]
  R37 = Resistor [tolerance=±5% resistance=1k package=THT]
  R38 = Resistor [tolerance=±5% resistance=1k package=THT]
  Q23 = NPN-Transistor [package="TO92 [THT]"]
  Q24 = NPN-Transistor [package="TO92 [THT]"]
  Q25 = NPN-Transistor [package="TO92 [THT]"]
  Q26 = NPN-Transistor [package="TO92 [THT]"]
  Q27 = PNP-Transistor [package="TO92 [THT]"]
  Q28 = PNP-Transistor [package="TO92 [THT]"]
  Q29 = PNP-Transistor [package="TO92 [THT]"]
  Q30 = PNP-Transistor [package="TO92 [THT]"]
  D40 = Rectifier Diode [part_number=1N4148 package="300 mil [THT]"]
  D41 = Rectifier Diode [part_number=1N4148 package="300 mil [THT]"]
  D42 = Rectifier Diode [part_number=1N4148 package="300 mil [THT]"]
  D43 = Rectifier Diode [part_number=1N4148 package="300 mil [THT]"]
  D44 = Rectifier Diode [part_number=1N4148 package="300 mil [THT]"]
  D45 = Rectifier Diode [part_number=1N4148 package="300 mil [THT]"]
  D46 = Rectifier Diode [part_number=1N4148 package="300 mil [THT]"]
  D47 = Rectifier Diode [part_number=1N4148 package="300 mil [THT]"]
  Coil1_M3 = Screw terminal - 2 pins [package=THT]
  Coil2_M3 = Screw terminal - 2 pins [package=THT]
  R39 = Resistor [tolerance=±5% resistance=1k package=THT]
  R40 = Resistor [tolerance=±5% resistance=1k package=THT]
  R41 = Resistor [tolerance=±5% resistance=1k package=THT]
  R42 = Resistor [tolerance=±5% resistance=1k package=THT]
  R43 = Resistor [tolerance=±5% resistance=1k package=THT]
  R44 = Resistor [tolerance=±5% resistance=1k package=THT]
  R45 = Resistor [tolerance=±5% resistance=1k package=THT]
  R46 = Resistor [tolerance=±5% resistance=1k package=THT]
  Q31 = NPN-Transistor [package="TO92 [THT]"]
  Q32 = NPN-Transistor [package="TO92 [THT]"]
  Q33 = NPN-Transistor [package="TO92 [THT]"]
  Q34 = NPN-Transistor [package="TO92 [THT]"]
  Q35 = PNP-Transistor [package="TO92 [THT]"]
  Q36 = PNP-Transistor [package="TO92 [THT]"]
  Q37 = PNP-Transistor [package="TO92 [THT]"]
  Q38 = PNP-Transistor [package="TO92 [THT]"]
  D48 = Rectifier Diode [part_number=1N4148 package="300 mil [THT]"]
  D49 = Rectifier Diode [part_number=1N4148 package="300 mil [THT]"]
  D50 = Rectifier Diode [part_number=1N4148 package="300 mil [THT]"]
  D51 = Rectifier Diode [part_number=1N4148 package="300 mil [THT]"]
  D52 = Rectifier Diode [part_number=1N4148 package="300 mil [THT]"]
  D53 = Rectifier Diode [part_number=1N4148 package="300 mil [THT]"]
  D54 = Rectifier Diode [part_number=1N4148 package="300 mil [THT]"]
  D55 = Rectifier Diode [part_number=1N4148 package="300 mil [THT]"]
  Coil1_M4 = Screw terminal - 2 pins [package=THT]
  Coil2_M4 = Screw terminal - 2 pins [package=THT]
  EXTRUDER = female pin header, 4 pins [form="♀ (female)"]
  Componente1 = Arduino Mega 2560 (Rev3)
  R47 = Resistor [tolerance=±5% resistance=330 package=THT]
  LED3 = LED - 5mm [color="Red (633nm)" package="5 mm [THT]"]

nets:
  temperatura HE: temp_HotEnd.pin1, R1.Pin_0, C1.+, Componente1.A13
  GND: temp_HotEnd.pin2, C1.-, C2.-, temp_HeatBed.pin2, Endstop_X.pin2, Endstop_Y.pin2, Endstop_Z1.pin2, Endstop_Z2.pin2, Fan1.pin2, Fan2.pin2, Heatbed.pin2, Hotend.pin2, LED1.cathode, LED2.cathode, ATX.pin2, ATX.pin3, Q7.E, Q9.E, D20.anode, D23.anode, D24.anode, D25.anode, D26.anode, D27.anode, Q11.E, Q12.E, D29.anode, D30.anode, Q15.E, Q16.E, Q17.E, Q18.E, D33.anode, D34.anode, D35.anode, D37.anode, Q23.E, Q24.E, Q25.E, Q26.E, D40.anode, D41.anode, D46.anode, D47.anode, Q31.E, Q32.E, Q33.E, Q34.E, D48.anode, D49.anode, D54.anode, D55.anode, LED3.cathode
  5V: R1.Pin_1, R2.Pin_1, ATX.pin4
  temperatura HB: R2.Pin_0, C2.+, temp_HeatBed.pin1, Componente1.A14
  ES X: Endstop_X.pin1, Componente1.D26
  ES Y: Endstop_Y.pin1, Componente1.D27
  ES Z1: Endstop_Z1.pin1, Componente1.D28
  ES Z2: Endstop_Z2.pin1, Componente1.D29
  N1: Fan1.pin1, Q5.E
  N2: Fan2.pin1, Q6.E
  N3: Heatbed.pin1, Q3.E, Q4.E, R10.Pin_0
  N4: Q1.E, Hotend.pin1
  N5: Q1.B, R3.Pin_1
  12V/Vin: Q1.C, Q2.C, Q5.C, Q6.C, ATX.pin1, R15.Pin_0, R16.Pin_0, R17.Pin_0, R18.Pin_0, Componente1.VIN
  N6: Q2.E, R9.Pin_0
  N7: Q2.B, R4.Pin_1
  HE: R3.Pin_0, R4.Pin_0, Componente1.D22
  N8: Q3.B, R5.Pin_1
  N9: Q3.C, Q4.C
  N10: Q4.B, R6.Pin_1
  HB: R5.Pin_0, R6.Pin_0, Componente1.D23
  N11: Q5.B, R7.Pin_1
  FAN1: R7.Pin_0, Componente1.D24
  FAN2: R8.Pin_0, Componente1.D25
  N12: R8.Pin_1, Q6.B
  N13: R9.Pin_1, LED1.anode
  N14: R10.Pin_1, LED2.anode
  N15: Q7.B, R12.Pin_1
  N16: Q7.C, Q8.C, D20.cathode, D21.anode, Coil1_M1.pin2
  7v1: Q8.E, Q10.E, D21.cathode, D22.cathode, Q13.E, Q14.E, D28.cathode, D31.cathode
  N17: Q8.B, R11.Pin_1
  N18: Q9.B, R14.Pin_0
  N19: Q9.C, Q10.C, D22.anode, D23.cathode, Coil1_M1.pin1
  N20: Q10.B, R13.Pin_0
  m1: R11.Pin_0, R12.Pin_0, Componente1.D30
  m2: R13.Pin_1, R14.Pin_1, Componente1.D31
  7V4: R15.Pin_1, D24.cathode
  7V3: R16.Pin_1, D25.cathode
  7V2: R17.Pin_1, D26.cathode
  7V1: R18.Pin_1, D27.cathode
  N21: R19.Pin_0, Q12.B
  m4: R19.Pin_1, R20.Pin_1, Componente1.D33
  N22: R20.Pin_0, Q14.B
  m3: R21.Pin_0, R22.Pin_0, Componente1.D32
  N23: R21.Pin_1, Q13.B
  N24: R22.Pin_1, Q11.B
  N25: Q11.C, Q13.C, D29.cathode, D31.anode, Coil2_M1.pin2
  N26: Q12.C, Q14.C, D28.anode, D30.cathode, Coil2_M1.pin1
  N27: R23.Pin_0, Q21.B
  m10: R23.Pin_1, R28.Pin_1, Componente1.D39
  N28: R24.Pin_0, Q22.B
  m12: R24.Pin_1, R30.Pin_1, Componente1.D41
  m9: R25.Pin_0, R26.Pin_0, Componente1.D38
  N29: R25.Pin_1, Q16.B
  N30: R26.Pin_1, Q20.B
  m11: R27.Pin_0, R29.Pin_0, Componente1.D40
  N31: R27.Pin_1, Q19.B
  N32: R28.Pin_0, Q15.B
  N33: R29.Pin_1, Q18.B
  N34: R30.Pin_0, Q17.B
  N35: Q15.C, Q21.C, D36.anode, D37.cathode, Coil1_M2.pin1
  N36: Q16.C, Q20.C, D33.cathode, D39.anode, Coil1_M2.pin2
  N37: Q17.C, Q22.C, D34.cathode, D38.anode, Coil2_M2.pin1
  N38: Q18.C, Q19.C, D32.anode, D35.cathode, Coil2_M2.pin2
  7v2: Q19.E, Q20.E, Q21.E, Q22.E, D32.cathode, D36.cathode, D38.cathode, D39.cathode
  m5: R31.Pin_0, R36.Pin_0, Componente1.D34
  N39: R31.Pin_1, Q26.B
  m7: R32.Pin_0, R34.Pin_0, Componente1.D36
  N40: R32.Pin_1, Q29.B
  N41: R33.Pin_0, Q23.B
  m6: R33.Pin_1, R35.Pin_1, Componente1.D35
  N42: R34.Pin_1, Q24.B
  N43: R35.Pin_0, Q27.B
  N44: R36.Pin_1, Q28.B
  N45: R37.Pin_0, Q30.B
  m8: R37.Pin_1, R38.Pin_1, Componente1.D37
  N46: R38.Pin_0, Q25.B
  N47: Q23.C, Q27.C, D44.anode, D46.cathode, Coil1_M3.pin1
  N48: Q24.C, Q29.C, D40.cathode, D43.anode, Coil2_M3.pin2
  N49: Q25.C, Q30.C, D41.cathode, D45.anode, Coil2_M3.pin1
  N50: Q26.C, Q28.C, D42.anode, D47.cathode, Coil1_M3.pin2
  7v3: Q27.E, Q28.E, Q29.E, Q30.E, D42.cathode, D43.cathode, D44.cathode, D45.cathode
  m13: R39.Pin_0, R44.Pin_0, Componente1.D42
  N51: R39.Pin_1, Q34.B
  m15: R40.Pin_0, R42.Pin_0, Componente1.D44
  N52: R40.Pin_1, Q37.B
  N53: R41.Pin_0, Q31.B
  m14: R41.Pin_1, R43.Pin_1, Componente1.D43
  N54: R42.Pin_1, Q32.B
  N55: R43.Pin_0, Q35.B
  N56: R44.Pin_1, Q36.B
  N57: R45.Pin_0, Q38.B
  m16: R45.Pin_1, R46.Pin_1, Componente1.D45
  N58: R46.Pin_0, Q33.B
  N59: Q31.C, Q35.C, D52.anode, D54.cathode, Coil1_M4.pin1
  N60: Q32.C, Q37.C, D48.cathode, D51.anode, Coil2_M4.pin2
  N61: Q33.C, Q38.C, D49.cathode, D53.anode, Coil2_M4.pin1
  N62: Q34.C, Q36.C, D50.anode, D55.cathode, Coil1_M4.pin2
  7v4: Q35.E, Q36.E, Q37.E, Q38.E, D50.cathode, D51.cathode, D52.cathode, D53.cathode
  m17: EXTRUDER.pin1, Componente1.D46
  m18: EXTRUDER.pin2, Componente1.D47
  m19: EXTRUDER.pin3, Componente1.D48
  m20: EXTRUDER.pin4, Componente1.D49
  printing: Componente1.D13_PWM, R47.Pin_0
  lcd rs: Componente1.D12_PWM
  lcd e: Componente1.D11_PWM
  lcd d4: Componente1.D10_PWM
  lcd d5: Componente1.D9_PWM
  lcd d6: Componente1.D8_PWM
  btn back: Componente1.D2_PWM
  buzzer: Componente1.D3_PWM
  btn ok: Componente1.D4_PWM
  btn down: Componente1.D5_PWM
  btn up: Componente1.D6_PWM
  lcd d7: Componente1.D7_PWM
  cart reader: Componente1.D50, Componente1.D51, Componente1.D52, Componente1.D53
  N63: R47.Pin_1, LED3.anode
